# Fritzing sketch wifi-scan (saved by Fritzing 0.9.3b)

parts:
  RGB_SMD_LED1 = SMD RGB LED (WS2812) [package=5050]
  M1 = RioRand LM2596
  RGB_SMD_LED2 = SMD RGB LED (WS2812) [package=5050]
  RGB_SMD_LED3 = SMD RGB LED (WS2812) [package=5050]
  RGB_SMD_LED4 = SMD RGB LED (WS2812) [package=5050]
  RGB_SMD_LED5 = SMD RGB LED (WS2812) [package=5050]
  RGB_SMD_LED6 = SMD RGB LED (WS2812) [package=5050]
  U1 = USB Connectors [package=usb-microb]
  U2 = ESP8266-12e_tht [part_number=ESP8266-12E]

nets:
  N1: RGB_SMD_LED1.DOut, M1.Pin_2, U1.GND
  N2: RGB_SMD_LED1.DIn, U2.GPIO_4
  N3: RGB_SMD_LED1.VCC, M1.Pin_1, U1.VBUS
  N4: RGB_SMD_LED1.NC, RGB_SMD_LED2.VCC
  N5: RGB_SMD_LED1.VDD, RGB_SMD_LED2.DIn
  N6: RGB_SMD_LED1.VSS, RGB_SMD_LED2.DOut
  N7: M1.Pin_3, U2.VCC
  N8: M1.Pin_4, U2.GND, U2.GPIO_15
  N9: RGB_SMD_LED2.NC, RGB_SMD_LED3.VCC
  N10: RGB_SMD_LED2.VDD, RGB_SMD_LED3.DIn
  N11: RGB_SMD_LED2.VSS, RGB_SMD_LED3.DOut
  N12: RGB_SMD_LED3.NC, RGB_SMD_LED4.VCC
  N13: RGB_SMD_LED3.VDD, RGB_SMD_LED4.DIn
  N14: RGB_SMD_LED3.VSS, RGB_SMD_LED4.DOut
  N15: RGB_SMD_LED4.NC, RGB_SMD_LED5.VCC
  N16: RGB_SMD_LED4.VDD, RGB_SMD_LED5.DIn
  N17: RGB_SMD_LED4.VSS, RGB_SMD_LED5.DOut
  N18: RGB_SMD_LED5.NC, RGB_SMD_LED6.VCC
  N19: RGB_SMD_LED5.VDD, RGB_SMD_LED6.DIn
  N20: RGB_SMD_LED5.VSS, RGB_SMD_LED6.DOut

custom parts:
  ESP8266-12e_tht: These are the first series of modules made with the ESP8266 by the third-party manufacturer AI-Thinker and remain the most widely available. They are collectively referred to as "ESP-xx modules" and to form a workable development system require additional components, especially a serial TTL-to-USB adapter (sometimes called a USB-to-UART bridge) and an external 3.3V power supply. The pcb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
